// Logisim project MIPS.circ as structural Verilog: 1 circuit, main circuit main
module main (
);

  wire and_1_out, clock_1_out, main_4_out_5, UC_Principal_alusrc, UC_Principal_branch, UC_Principal_memread,
       UC_Principal_memtoreg, UC_Principal_memwrite, UC_Principal_regdst, UC_Principal_regwrite;
  wire [1:0] UC_Principal_aluop;
  wire [2:0] main_2_op_2;
  wire [4:0] multiplexer_1_out;
  wire [31:0] bit_extender_1_out, main_1_out_6, main_3_out_6, main_4_out_6, Memoria_de_Dados_read_data,
       \Memoria_de_Instrução_instruction , multiplexer_2_out, multiplexer_3_out, multiplexer_4_out,
       n32_register_file_1_read_data_2, PC_q, shifter_1_out;

  Counter #(.width(32), .max('hffffffff)) PC (
    .D(multiplexer_3_out), .Q(PC_q), .clk(clock_1_out));  // open: load, count, carry, clr
  Clock clock_1 (.out(clock_1_out));
  Instruction_Memory \Memoria_de_Instrução  (.Read_Address(PC_q), .Instruction(\Memoria_de_Instrução_instruction ));
  Ula_32BITS_main main_1 (.in_3(32'h4), .in_4(PC_q), .out_6(main_1_out_6));  // open: out_5, bInvert, in_1, Overflow
  Multiplexer #(.width(5), .enable("false")) multiplexer_1 (
    .in0(\Memoria_de_Instrução_instruction [20:16]), .in1(\Memoria_de_Instrução_instruction [15:11]),
    .out(multiplexer_1_out), .sel(UC_Principal_regdst));
  UC_Principal_main UC_Principal (
    .in_1(\Memoria_de_Instrução_instruction [31:26]), .RegDst(UC_Principal_regdst),
    .ALUSrc(UC_Principal_alusrc), .MemtoReg(UC_Principal_memtoreg), .RegWrite(UC_Principal_regwrite),
    .MemRead(UC_Principal_memread), .MemWrite(UC_Principal_memwrite), .Branch(UC_Principal_branch),
    .ALUOP(UC_Principal_aluop));
  assign bit_extender_1_out = {{16{1'b0}}, \Memoria_de_Instrução_instruction [15:0]};  // Bit_Extender bit_extender_1
  _32_register_file u_32_register_file_1 (
    .Read_Register_1(\Memoria_de_Instrução_instruction [25:21]),
    .Read_Register_2(\Memoria_de_Instrução_instruction [20:16]), .Write_Register(multiplexer_1_out),
    .Write_Data_2(multiplexer_4_out), .Write_Data(UC_Principal_regwrite),
    .Read_Data_2(n32_register_file_1_read_data_2));  // open: Read_data_1
  Shifter #(.width(32)) shifter_1 (.in(bit_extender_1_out), .\dist ({5{1'b0}}), .out(shifter_1_out));
  Multiplexer #(.width(32), .enable("false")) multiplexer_2 (
    .in0(n32_register_file_1_read_data_2), .in1(bit_extender_1_out), .out(multiplexer_2_out),
    .sel(UC_Principal_alusrc));
  UC_Ula_main main_2 (.Funct(\Memoria_de_Instrução_instruction [5:0]), .OP(UC_Principal_aluop), .Op_2(main_2_op_2));
  Ula_32BITS_main main_3 (
    .in_3(main_1_out_6), .in_4(shifter_1_out), .bInvert(1'b0), .in_1(3'b010), .out_6(main_3_out_6));  // open: out_5, Overflow
  Ula_32BITS_main main_4 (
    .in_4(multiplexer_2_out), .out_5(main_4_out_5), .in_1(main_2_op_2), .out_6(main_4_out_6));  // open: in_3, bInvert, Overflow
  and and_1 (and_1_out, UC_Principal_branch, main_4_out_5);
  Data_Memory Memoria_de_Dados (
    .Address(main_4_out_6), .Write_Data(n32_register_file_1_read_data_2), .Mem_Write(UC_Principal_memwrite),
    .Read_Enable(UC_Principal_memread), .Read_Data(Memoria_de_Dados_read_data));
  Multiplexer #(.width(32), .enable("false")) multiplexer_3 (
    .in0(main_1_out_6), .in1(main_3_out_6), .out(multiplexer_3_out), .sel(and_1_out));
  Multiplexer #(.width(32), .enable("false")) multiplexer_4 (
    .in0(main_4_out_6), .in1(Memoria_de_Dados_read_data), .out(multiplexer_4_out), .sel(UC_Principal_memtoreg));
endmodule
