// Logisim project UC-Principal.circ as structural Verilog: 1 circuit, main circuit main
module main (
  input  [5:0] in_1,
  output RegDst,
  output ALUSrc,
  output MemtoReg,
  output RegWrite,
  output MemRead,
  output MemWrite,
  output Branch,
  output [1:0] ALUOP
);

  and R_format (ALUOP[1], ~in_1[0], ~in_1[1], ~in_1[2], ~in_1[3], ~in_1[4], ~in_1[5]);  // AND_Gate
  and lw (MemRead, in_1[0], ~in_1[1], ~in_1[2], ~in_1[3], in_1[4], in_1[5]);  // AND_Gate
  and sw (MemWrite, in_1[0], ~in_1[1], in_1[2], ~in_1[3], in_1[4], in_1[5]);  // AND_Gate
  and beq (ALUOP[0], ~in_1[0], ~in_1[1], ~in_1[2], in_1[3], ~in_1[4], ~in_1[5]);  // AND_Gate
  or or_1 (ALUSrc, MemRead, MemWrite);
  or or_2 (RegWrite, ALUOP[1], MemRead);

  assign Branch = ALUOP[0];
  assign MemtoReg = MemRead;
  assign RegDst = ALUOP[1];
endmodule
