// Logisim project UC-Ula.circ as structural Verilog: 1 circuit, main circuit main
module main (
  input  [1:0] OP,
  input  [5:0] Funct,
  output [2:0] Op_2
);

  wire and_1_out, or_1_out;

  or or_1 (or_1_out, Funct[3], Funct[0]);
  and and_1 (and_1_out, OP[1], Funct[1]);
  and and_2 (Op_2[0], OP[1], or_1_out);
  or or_2 (Op_2[2], OP[0], and_1_out);
  or or_3 (Op_2[1], ~OP[1], ~Funct[2]);  // OR_Gate
endmodule
