// Logisim project Ula-1bit.circ as structural Verilog: 1 circuit, main circuit main
module main (
  input  aInvert,
  input  bInvert,
  input  CarryIn,
  input  [1:0] Operacao,
  input  a,
  input  b,
  input  Less,
  output Resultado,
  output CarryOut
);

  wire and_1_out, main_1_soma, multiplexer_1_out, multiplexer_2_out, not_1_out, not_2_out, or_1_out;

  not not_1 (not_1_out, a);
  not not_2 (not_2_out, b);
  Multiplexer multiplexer_1 (.in0(a), .in1(not_1_out), .out(multiplexer_1_out), .sel(aInvert));  // open: en
  Multiplexer multiplexer_2 (.in0(b), .in1(not_2_out), .out(multiplexer_2_out), .sel(bInvert));  // open: en
  and and_1 (and_1_out, multiplexer_1_out, multiplexer_2_out);
  or or_1 (or_1_out, multiplexer_1_out, multiplexer_2_out);
  somador_main main_1 (
    .a(multiplexer_1_out), .b(multiplexer_2_out), .CarryIn(CarryIn), .CarryOut(CarryOut), .Soma(main_1_soma));
  Multiplexer #(.select(2)) multiplexer_3 (
    .in0(and_1_out), .in1(or_1_out), .in2(main_1_soma), .in3(Less), .out(Resultado), .sel(Operacao));  // open: en
endmodule
