// Logisim project Ula-32BITS.circ as structural Verilog: 1 circuit, main circuit main
module main (
  input  [2:0] in_1,
  input  bInvert,
  input  [31:0] in_3,
  input  [31:0] in_4,
  output out_5,
  output Overflow
);

  wire main_1_carryout, main_1_resultado, main_2_carryout, main_2_resultado, main_3_carryout,
       main_3_resultado, main_4_carryout, main_4_resultado, main_5_carryout, main_5_resultado,
       main_6_carryout, main_6_resultado, main_7_carryout, main_7_resultado, main_8_carryout,
       main_8_resultado, main_9_carryout, main_9_resultado, main_10_carryout, main_10_resultado,
       main_11_carryout, main_11_resultado, main_12_carryout, main_12_resultado, main_13_carryout,
       main_13_resultado, main_14_carryout, main_14_resultado, main_15_carryout, main_15_resultado,
       main_16_carryout, main_16_resultado, main_17_carryout, main_17_resultado, main_18_carryout,
       main_18_resultado, main_19_carryout, main_19_resultado, main_20_carryout, main_20_resultado,
       main_21_carryout, main_21_resultado, main_22_carryout, main_22_resultado, main_23_carryout,
       main_23_resultado, main_24_carryout, main_24_resultado, main_25_carryout, main_25_resultado,
       main_26_carryout, main_26_resultado, main_27_carryout, main_27_resultado, main_28_carryout,
       main_28_resultado, main_29_carryout, main_29_resultado, main_30_carryout, main_30_resultado,
       main_31_carryout, main_31_resultado, main_32_resultado, main_32_set, or_1_out;

  Ula_1bit_main main_1 (
    .a(in_3[0]), .b(in_4[0]), .Less(main_32_set), .Resultado(main_1_resultado), .bInvert(bInvert),
    .CarryIn(bInvert), .Operacao(in_1[1:0]), .CarryOut(main_1_carryout));
  Ula_1bit_main main_2 (
    .a(in_3[1]), .b(in_4[1]), .Less(1'b0), .Resultado(main_2_resultado), .bInvert(bInvert),
    .CarryIn(main_1_carryout), .Operacao(in_1[1:0]), .CarryOut(main_2_carryout));
  Ula_1bit_main main_3 (
    .a(in_3[2]), .b(in_4[2]), .Less(1'b0), .Resultado(main_3_resultado), .bInvert(bInvert),
    .CarryIn(main_2_carryout), .Operacao(in_1[1:0]), .CarryOut(main_3_carryout));
  Ula_1bit_main main_4 (
    .a(in_3[3]), .b(in_4[3]), .Less(1'b0), .Resultado(main_4_resultado), .bInvert(bInvert),
    .CarryIn(main_3_carryout), .Operacao(in_1[1:0]), .CarryOut(main_4_carryout));
  Ula_1bit_main main_5 (
    .a(in_3[4]), .b(in_4[4]), .Less(1'b0), .Resultado(main_5_resultado), .bInvert(bInvert),
    .CarryIn(main_4_carryout), .Operacao(in_1[1:0]), .CarryOut(main_5_carryout));
  Ula_1bit_main main_6 (
    .a(in_3[5]), .b(in_4[5]), .Less(1'b0), .Resultado(main_6_resultado), .bInvert(bInvert),
    .CarryIn(main_5_carryout), .Operacao(in_1[1:0]), .CarryOut(main_6_carryout));
  Ula_1bit_main main_7 (
    .a(in_3[6]), .b(in_4[6]), .Less(1'b0), .Resultado(main_7_resultado), .bInvert(bInvert),
    .CarryIn(main_6_carryout), .Operacao(in_1[1:0]), .CarryOut(main_7_carryout));
  Ula_1bit_main main_8 (
    .a(in_3[7]), .b(in_4[7]), .Less(1'b0), .Resultado(main_8_resultado), .bInvert(bInvert),
    .CarryIn(main_7_carryout), .Operacao(in_1[1:0]), .CarryOut(main_8_carryout));
  Ula_1bit_main main_9 (
    .a(in_3[8]), .b(in_4[8]), .Less(1'b0), .Resultado(main_9_resultado), .bInvert(bInvert),
    .CarryIn(main_8_carryout), .Operacao(in_1[1:0]), .CarryOut(main_9_carryout));
  Ula_1bit_main main_10 (
    .a(in_3[9]), .b(in_4[9]), .Less(1'b0), .Resultado(main_10_resultado), .bInvert(bInvert),
    .CarryIn(main_9_carryout), .Operacao(in_1[1:0]), .CarryOut(main_10_carryout));
  Ula_1bit_main main_11 (
    .a(in_3[10]), .b(in_4[10]), .Less(1'b0), .Resultado(main_11_resultado), .bInvert(bInvert),
    .CarryIn(main_10_carryout), .Operacao(in_1[1:0]), .CarryOut(main_11_carryout));
  Ula_1bit_main main_12 (
    .a(in_3[11]), .b(in_4[11]), .Less(1'b0), .Resultado(main_12_resultado), .bInvert(bInvert),
    .CarryIn(main_11_carryout), .Operacao(in_1[1:0]), .CarryOut(main_12_carryout));
  Ula_1bit_main main_13 (
    .a(in_3[12]), .b(in_4[12]), .Less(1'b0), .Resultado(main_13_resultado), .bInvert(bInvert),
    .CarryIn(main_12_carryout), .Operacao(in_1[1:0]), .CarryOut(main_13_carryout));
  Ula_1bit_main main_14 (
    .a(in_3[13]), .b(in_4[13]), .Less(1'b0), .Resultado(main_14_resultado), .bInvert(bInvert),
    .CarryIn(main_13_carryout), .Operacao(in_1[1:0]), .CarryOut(main_14_carryout));
  Ula_1bit_main main_15 (
    .a(in_3[14]), .b(in_4[14]), .Less(1'b0), .Resultado(main_15_resultado), .bInvert(bInvert),
    .CarryIn(main_14_carryout), .Operacao(in_1[1:0]), .CarryOut(main_15_carryout));
  Ula_1bit_main main_16 (
    .a(in_3[15]), .b(in_4[15]), .Less(1'b0), .Resultado(main_16_resultado), .bInvert(bInvert),
    .CarryIn(main_15_carryout), .Operacao(in_1[1:0]), .CarryOut(main_16_carryout));
  Ula_1bit_main main_17 (
    .a(in_3[16]), .b(in_4[16]), .Less(1'b0), .Resultado(main_17_resultado), .bInvert(bInvert),
    .CarryIn(main_16_carryout), .Operacao(in_1[1:0]), .CarryOut(main_17_carryout));
  Ula_1bit_main main_18 (
    .a(in_3[17]), .b(in_4[17]), .Less(1'b0), .Resultado(main_18_resultado), .bInvert(bInvert),
    .CarryIn(main_17_carryout), .Operacao(in_1[1:0]), .CarryOut(main_18_carryout));
  Ula_1bit_main main_19 (
    .a(in_3[18]), .b(in_4[18]), .Less(1'b0), .Resultado(main_19_resultado), .bInvert(bInvert),
    .CarryIn(main_18_carryout), .Operacao(in_1[1:0]), .CarryOut(main_19_carryout));
  Ula_1bit_main main_20 (
    .a(in_3[19]), .b(in_4[19]), .Less(1'b0), .Resultado(main_20_resultado), .bInvert(bInvert),
    .CarryIn(main_19_carryout), .Operacao(in_1[1:0]), .CarryOut(main_20_carryout));
  Ula_1bit_main main_21 (
    .a(in_3[20]), .b(in_4[20]), .Less(1'b0), .Resultado(main_21_resultado), .bInvert(bInvert),
    .CarryIn(main_20_carryout), .Operacao(in_1[1:0]), .CarryOut(main_21_carryout));
  Ula_1bit_main main_22 (
    .a(in_3[21]), .b(in_4[21]), .Less(1'b0), .Resultado(main_22_resultado), .bInvert(bInvert),
    .CarryIn(main_21_carryout), .Operacao(in_1[1:0]), .CarryOut(main_22_carryout));
  Ula_1bit_main main_23 (
    .a(in_3[22]), .b(in_4[22]), .Less(1'b0), .Resultado(main_23_resultado), .bInvert(bInvert),
    .CarryIn(main_22_carryout), .Operacao(in_1[1:0]), .CarryOut(main_23_carryout));
  Ula_1bit_main main_24 (
    .a(in_3[23]), .b(in_4[23]), .Less(1'b0), .Resultado(main_24_resultado), .bInvert(bInvert),
    .CarryIn(main_23_carryout), .Operacao(in_1[1:0]), .CarryOut(main_24_carryout));
  Ula_1bit_main main_25 (
    .a(in_3[24]), .b(in_4[24]), .Less(1'b0), .Resultado(main_25_resultado), .bInvert(bInvert),
    .CarryIn(main_24_carryout), .Operacao(in_1[1:0]), .CarryOut(main_25_carryout));
  Ula_1bit_main main_26 (
    .a(in_3[25]), .b(in_4[25]), .Less(1'b0), .Resultado(main_26_resultado), .bInvert(bInvert),
    .CarryIn(main_25_carryout), .Operacao(in_1[1:0]), .CarryOut(main_26_carryout));
  Ula_1bit_main main_27 (
    .a(in_3[26]), .b(in_4[26]), .Less(1'b0), .Resultado(main_27_resultado), .bInvert(bInvert),
    .CarryIn(main_26_carryout), .Operacao(in_1[1:0]), .CarryOut(main_27_carryout));
  Ula_1bit_main main_28 (
    .a(in_3[27]), .b(in_4[27]), .Less(1'b0), .Resultado(main_28_resultado), .bInvert(bInvert),
    .CarryIn(main_27_carryout), .Operacao(in_1[1:0]), .CarryOut(main_28_carryout));
  Ula_1bit_main main_29 (
    .a(in_3[28]), .b(in_4[28]), .Less(1'b0), .Resultado(main_29_resultado), .bInvert(bInvert),
    .CarryIn(main_28_carryout), .Operacao(in_1[1:0]), .CarryOut(main_29_carryout));
  Ula_1bit_main main_30 (
    .a(in_3[29]), .b(in_4[29]), .Less(1'b0), .Resultado(main_30_resultado), .bInvert(bInvert),
    .CarryIn(main_29_carryout), .Operacao(in_1[1:0]), .CarryOut(main_30_carryout));
  Ula_1bit_main main_31 (
    .a(in_3[30]), .b(in_4[30]), .Less(1'b0), .Resultado(main_31_resultado), .bInvert(bInvert),
    .CarryIn(main_30_carryout), .Operacao(in_1[1:0]), .CarryOut(main_31_carryout));
  Ula_32bit_main main_32 (
    .a(in_3[31]), .b(in_4[31]), .Less(1'b0), .Resultado(main_32_resultado), .Set(main_32_set),
    .bInvert(bInvert), .CarryIn(main_31_carryout), .Operacao(in_1[1:0]), .CarryOut(Overflow));
  or or_1 (or_1_out, main_1_resultado, main_2_resultado, main_3_resultado, main_4_resultado, main_5_resultado, main_6_resultado, main_7_resultado, main_8_resultado, main_9_resultado, main_10_resultado, main_11_resultado, main_12_resultado, main_13_resultado, main_14_resultado, main_15_resultado, main_16_resultado, main_17_resultado, main_18_resultado, main_19_resultado, main_20_resultado, main_21_resultado, main_22_resultado, main_23_resultado, main_24_resultado, main_25_resultado, main_26_resultado, main_27_resultado, main_28_resultado, main_29_resultado, main_30_resultado, main_31_resultado, main_32_resultado);
  not not_1 (out_5, or_1_out);

  assign in_1[2] = bInvert;
endmodule
