// Logisim project somador.circ as structural Verilog: 1 circuit, main circuit main
module main (
  input  CarryIn,
  input  a,
  input  b,
  output Soma,
  output CarryOut
);

  wire and_1_out, and_2_out, and_3_out, xor_1_out;

  xor xor_1 (xor_1_out, a, b);
  and and_1 (and_1_out, a, b);
  and and_2 (and_2_out, a, CarryIn);
  and and_3 (and_3_out, b, CarryIn);
  xor xor_2 (Soma, xor_1_out, CarryIn);
  or or_1 (CarryOut, and_1_out, and_2_out, and_3_out);
endmodule
